# Fritzing sketch IoT (saved by Fritzing 0.9.3b)
breadboards: 1

parts:
  Uploader = WeMos D1 Mini
  RHT1 = Humidity and Temperature Sensor RHT03
  Downloader = WeMos D1 Mini
  Device = Arduino Uno (Rev3)
  R1 = Resistor [tolerance=±5% resistance=1k package=THT]
  R2 = Resistor [tolerance=±5% resistance=10k package=THT]
  C1 = Ceramic Capacitor [capacitance=1µF package="100 mil [THT, multilayer]"]
  U1 = 555 Timer [package="DIP8 [THT]"]
  J1 = Piezo Speaker

nets:
  3V3: Uploader.3V3, RHT1.Vcc
  N1: Uploader.D5, RHT1.Data-signal
  N2: Uploader.G, RHT1.GND_2
  N3: Downloader.D4, Device.D2
  N4: Device.D8, U1.Reset
  N5: Device.3V3, R1.Pin_1, U1.Vcc_Supply_Voltage
  N6: Device.GND, C1.0, U1.Ground, J1.pin2
  N7: R1.Pin_0, R2.Pin_1, U1.Discharge
  N8: R2.Pin_0, C1.1, U1.Trigger, U1.Threshold
  N9: U1.Output, J1.pin1

notes:
  Uploader - wemos D1 mini
  Downloader - nodeMCU
  Ambele microcontrollere se folosesc de modulul wifi esp8266.
  Uploader preia datele de la sensor la fiecare 10 secunde, iar la fiecare 300 secunde(5 minute),
  face media lor si le incarca.
  Downloader, la fiecare 300 secunde, descarca ultimele inregistrari si le transmite prin Serial (folosing protocolul UART). Aceastra transmitere este de tip SofwareSerial, deoarece pinii TX si RX, atata la Uno cat si la nodeMCU sunt cuplati la Serial Monitor in Arduino IDE si nu am vrut sa intervin asupra lor.
  Numaratoarea secundelor se realizeaza cu un timer.
  Incarcarea si descarcarea se face de pe canalul:
  https://thingspeak.com/channels/844317,
  prin utilizarea de query-uri HTTP.
  Probleme intampinate:
  1. In timere, in functia de intrerupere efectuam citirea sensorului, deci tineam procesorul prea mult in intrerupere, astfel placuta se reseta mereu cand se efectua intreruperea. Rezolvare: Creearea unor variable ce sunt incrementate in timer, si verificarea cu continuos polling in main loop .
  2. Transmiterea seriala corupea uneori date. Rezolvare:
  Incadrarea valorilor de transmis astfel : <temp,hum>,
  si verificarea acestora in valorile limita, adica:
  -20 < temp < 80 si 0 < hum < 100
  Timer 555 folosit in modul astabil pentru a controla un buzzer, in vederea obtinerii unui semnal ce va alterna si va produce zgomot in buzzer.
  Pinul Reset este controlat de Arduino pentru a initializa timer-ul, cat si pentru a-l opri.
